// Digital circuit MUX.dig as structural Verilog
module MUX (
  input  D,
  input  C,
  input  B,
  input  A,
  output Y
);

  wire not_1_out;

  not not_1 (not_1_out, D);
  Multiplexer #(.Selector_Bits(3)) multiplexer_1 (
    .sel({A, B, C}), .in_0(D), .in_1(D), .in_2(D), .in_3(D), .in_4(not_1_out), .in_5(not_1_out),
    .in_6(not_1_out), .in_7(1'b0), .out(Y));
endmodule

/* Test case:
A B C D Y
0 0 0 0 X
0 0 0 1 1
*/
